// Logisim project Practica 4.circ as structural Verilog: 4 circuits, main circuit Sumador 1 bit
module Sumador_1_bit (
  input  in_1,
  input  Y,
  input  C_in,
  output out_4,
  output Sum
);

  wire and_1_out, and_2_out, xor_1_out;

  and and_1 (and_1_out, in_1, Y);
  xor xor_1 (xor_1_out, in_1, Y);
  and and_2 (and_2_out, xor_1_out, C_in);
  xor xor_2 (Sum, xor_1_out, C_in);
  or or_1 (out_4, and_1_out, and_2_out);

  // Notes on the sheet:
  //   X
  //   SUMADOR DE 1 BIT
  //   C out
endmodule

module Sumador_de_8_bits (
  input  in_1,
  input  [7:0] in_2,
  input  [7:0] in_3,
  output [7:0] out_4,
  output out_5
);

  wire sumador_1_bit_1_out_4, sumador_1_bit_2_out_4, sumador_1_bit_3_out_4, sumador_1_bit_4_out_4,
       sumador_1_bit_5_out_4, sumador_1_bit_6_out_4, sumador_1_bit_7_out_4;

  Sumador_1_bit sumador_1_bit_1 (
    .in_1(in_2[0]), .Y(in_3[0]), .C_in(in_1), .out_4(sumador_1_bit_1_out_4), .Sum(out_4[0]));
  Sumador_1_bit sumador_1_bit_2 (
    .in_1(in_2[1]), .Y(in_3[1]), .C_in(sumador_1_bit_1_out_4), .out_4(sumador_1_bit_2_out_4), .Sum(out_4[1]));
  Sumador_1_bit sumador_1_bit_3 (
    .in_1(in_2[2]), .Y(in_3[2]), .C_in(sumador_1_bit_2_out_4), .out_4(sumador_1_bit_3_out_4), .Sum(out_4[2]));
  Sumador_1_bit sumador_1_bit_4 (
    .in_1(in_2[3]), .Y(in_3[3]), .C_in(sumador_1_bit_3_out_4), .out_4(sumador_1_bit_4_out_4), .Sum(out_4[3]));
  Sumador_1_bit sumador_1_bit_5 (
    .in_1(in_2[4]), .Y(in_3[4]), .C_in(sumador_1_bit_4_out_4), .out_4(sumador_1_bit_5_out_4), .Sum(out_4[4]));
  Sumador_1_bit sumador_1_bit_6 (
    .in_1(in_2[5]), .Y(in_3[5]), .C_in(sumador_1_bit_5_out_4), .out_4(sumador_1_bit_6_out_4), .Sum(out_4[5]));
  Sumador_1_bit sumador_1_bit_7 (
    .in_1(in_2[6]), .Y(in_3[6]), .C_in(sumador_1_bit_6_out_4), .out_4(sumador_1_bit_7_out_4), .Sum(out_4[6]));
  Sumador_1_bit sumador_1_bit_8 (
    .in_1(in_2[7]), .Y(in_3[7]), .C_in(sumador_1_bit_7_out_4), .out_4(out_5), .Sum(out_4[7]));

  // Notes on the sheet:
  //   C in
  //   X
  //   Y
  //   ACARREO DE SALIDA
endmodule

module Complemento_a_1 (
  input  [7:0] in_1,
  output [7:0] out_2
);

  not not_1 (out_2[0], in_1[0]);
  not not_2 (out_2[1], in_1[1]);
  not not_3 (out_2[2], in_1[2]);
  not not_4 (out_2[3], in_1[3]);
  not not_5 (out_2[4], in_1[4]);
  not not_6 (out_2[5], in_1[5]);
  not not_7 (out_2[6], in_1[6]);
  not not_8 (out_2[7], in_1[7]);

  // Notes on the sheet:
  //   B
endmodule

module Restador_de_8_bits (
  input  [7:0] in_1,
  input  [7:0] in_2,
  output [7:0] out_3,
  output out_4
);

  wire [7:0] complemento_a_1_1_out_2;

  Complemento_a_1 complemento_a_1_1 (.in_1(in_2), .out_2(complemento_a_1_1_out_2));
  Sumador_de_8_bits sumador_de_8_bits_1 (
    .in_1(1'b1), .in_2(in_1), .in_3(complemento_a_1_1_out_2), .out_4(out_3), .out_5(out_4));

  // Notes on the sheet:
  //   SUMA DE X + Y COMP A 1 + 1
  //   X
  //   Y
  //   SUMA DE 1 BIT PARA PASAR COMPLEMENTO A 1 -> COMPLEMENTO A 2 
  //   ACARREO DE SALIDA
  //   PASAMOS Y A COMPLEMENTO A 1
endmodule
